# Fritzing sketch WaterController (saved by Fritzing 0.9.3b)
breadboards: 1

parts:
  Raspberry_Pi_1 = Raspberry Pi 3 [part_number=RPI-3-V1.2]
  Part1 = Adafruit ADS1115 16Bit I2C ADC [part_number="Adafruit #1085"]
  C1 = Electrolytic Capacitor [capacitance=6.8µF package="0807 [SMD, electrolytic]"]
  J1 = Camdenboss CTB0158-3 [part_number=CTB0158-3 package=THT]
  Part2 = Soil Moisture Sensor [part_number="Vegetronix VH400"]
  Part3 = Soil Moisture Sensor [part_number="Seeedstudio Grove Moisture Sensor"]
  R2 = Resistor [tolerance=±5% resistance=10k package="2512 [SMD]"]
  R3 = Resistor [tolerance=±5% resistance=4.7k package="2512 [SMD]"]
  U1 = 4-Channel 5v Relay Shield [package=relay-4ch5v10a]

nets:
  3V3: Raspberry_Pi_1.3v3, Part1.VDD, C1.+, R2.Pin_1
  N1: Raspberry_Pi_1.GPIO2, Part1.SDA
  N2: Raspberry_Pi_1.GPIO3, Part1.SCL
  N3: Raspberry_Pi_1.GIPO17, U1.IN3
  N4: Raspberry_Pi_1.GIPO18, U1.IN4
  GND: Raspberry_Pi_1.GND, Part1.GND, C1.-, J1.pin2, Part2.GND, Part3.GND, R3.Pin_0
  VCC: Raspberry_Pi_1.5V, J1.pin1, Part2.VCC, Part3.VCC
  N5: Part1.AIN3, J1.pin3, Part2.SIG
  N6: Part1.AIN2, Part3.SIG
  N7: Part1.AIN1, R2.Pin_0, R3.Pin_1

notes:
  Value not too important
  To larger 5V supply (Not RPI's). I've tested with a 5V 1A supply, but smaller may work -- but not much smaller!

custom parts:
  Adafruit ADS1115 16Bit I2C ADC: For microcontrollers without an analog-to-digital converter or when you want a higher-precision ADC, the ADS1115 provides 16-bit precision at 860 samples/second over I2C. The chip can be configured as 4 single-ended input channels, or two differential channels. As a nice bonus, it even includes a programmable gain amplifier, up to x16, to help boost up smaller single/differential signals to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
  4-Channel 5v Relay Shield: 4 Channel 5v Relay Shield w. 2x SPD-06VDC-SD-C
